# Fritzing sketch Schaltplan (saved by Fritzing 0.8.7b)
breadboards: 1

parts:
  Bauteil1 = Arduino Mega ADK (Rev3)
  R4 = Resistor [tolerance=±5% resistance=1k package="0603 [SMD]"]
  R3 = Resistor [tolerance=±5% resistance=1k package="0603 [SMD]"]
  R2 = Resistor [tolerance=±5% resistance=1k package="0603 [SMD]"]
  R1 = Resistor [tolerance=±5% resistance=1k package="0603 [SMD]"]
  U1 = 7-SEGMENT-4DIGIT [package=7-segment-4digit-youngsun]
  S1 = Pushbutton [package="[THT]"]
  S2 = Pushbutton [package="[THT]"]
  S3 = Pushbutton [package="[THT]"]
  U3 = 7-SEGMENT-DISPLAY [package=7-segment-display]
  R5 = Resistor [tolerance=±5% resistance=1k package="0603 [SMD]"]
  J1 = Piezo Speaker

nets:
  N1: Bauteil1.D13_PWM, U1.5
  N2: Bauteil1.D12_PWM, U1.7
  N3: Bauteil1.D10_PWM, U1.3
  N4: Bauteil1.D9_PWM, U1.4
  N5: Bauteil1.D8_PWM, U1.6
  N6: Bauteil1.D2_PWM, R1.Pin_1
  N7: Bauteil1.D3_PWM, R2.Pin_1
  N8: Bauteil1.D4_PWM, R3.Pin_1
  N9: Bauteil1.D5_PWM, R4.Pin_1
  N10: Bauteil1.D6_PWM, U1.13
  N11: Bauteil1.D7_PWM, U1.9
  N12: Bauteil1.D22, S1.Pin_3
  N13: Bauteil1.D24, S2.Pin_3, S2.Pin_4
  N14: Bauteil1.D26, S3.Pin_3, S3.Pin_4
  N15: Bauteil1.D28, U3.D
  N16: Bauteil1.D30, R5.Pin_0
  N17: Bauteil1.D32, U3.G1
  N18: Bauteil1.D34, U3.DP
  N19: Bauteil1.D36, U3.B
  N20: Bauteil1.D38, U3.A
  N21: Bauteil1.D41, U3.F
  N22: Bauteil1.D43, U3.G
  N23: Bauteil1.D45, U3.E
  N24: R4.Pin_0, U1.8
  N25: R2.Pin_0, U1.11
  N26: R1.Pin_0, U1.14
  N27: S1.Pin_1, S1.Pin_2, S2.Pin_1, S2.Pin_2, S3.Pin_1, S3.Pin_2, J1.pin1
  N28: U3.C, U3.G2, R5.Pin_1
